// Logisim project 6651071076_LAB1_3.circ as structural Verilog: 2 circuits, main circuit main
module main (
  input  b0,
  input  b1,
  input  b2,
  input  b3,
  output out_5,
  output out_6,
  output out_7,
  output out_8
);

  wire fulladder1bit_1_sum, fulladder1bit_2_cout, fulladder1bit_3_cout, undriven, undriven_2, undriven_3,
       undriven_4;

  FullAdder1bit fulladder1bit_1 (
    .A(undriven_4), .Sum(fulladder1bit_1_sum), .Cout(fulladder1bit_1_sum));  // open: B, Cin
  FullAdder1bit fulladder1bit_2 (
    .A(fulladder1bit_1_sum), .B(undriven_2), .Sum(out_6), .Cout(fulladder1bit_2_cout));  // open: Cin
  FullAdder1bit fulladder1bit_3 (
    .A(fulladder1bit_2_cout), .B(undriven), .Sum(out_7), .Cout(fulladder1bit_3_cout));  // open: Cin
  FullAdder1bit fulladder1bit_4 (
    .A(fulladder1bit_3_cout), .Cin(undriven_3), .Sum(out_8), .Cout(fulladder1bit_1_sum));  // open: B
  // also tied to VCC on the sheet: fulladder1bit_1_sum
endmodule

module FullAdder1bit (
  input  A,
  input  B,
  input  Cin,
  output Sum,
  output Cout
);

  wire and_1_out, and_2_out, and_3_out, and_4_out, and_5_out, and_6_out, and_7_out, not_1_out, not_2_out,
       not_3_out, not_4_out, not_5_out, not_6_out;

  not not_1 (not_1_out, A);
  not not_2 (not_2_out, B);
  not not_3 (not_3_out, A);
  not not_4 (not_4_out, Cin);
  not not_5 (not_5_out, B);
  not not_6 (not_6_out, Cin);
  and and_1 (and_1_out, B, Cin);
  and and_2 (and_2_out, A, Cin);
  and and_3 (and_3_out, A, B);
  and and_4 (and_4_out, not_1_out, not_2_out, Cin);
  and and_5 (and_5_out, not_3_out, B, not_4_out);
  and and_6 (and_6_out, A, not_5_out, not_6_out);
  and and_7 (and_7_out, A, B, Cin);
  or or_1 (Cout, and_1_out, and_2_out, and_3_out);
  or or_2 (Sum, and_4_out, and_5_out, and_6_out, and_7_out);
endmodule
