// Logisim project 6651071076_LAB1_4.circ as structural Verilog: 2 circuits, main circuit main
module main (
  input  a1,
  input  b1,
  input  a2,
  input  b2,
  input  a3,
  input  b3,
  input  a4,
  input  b4,
  output sum1,
  output sum2,
  output sum3,
  output cout,
  output sum4
);

  wire b0_cout, b1_cout, b2_cout, b2_sum, b3_sum, undriven, undriven_2, undriven_3, undriven_4;

  FullAdder1bit b0 (.a(a1), .cin(undriven_4), .sum(sum1), .cout(b0_cout));  // open: b
  FullAdder1bit u_b1 (.a(b0_cout), .b(undriven), .sum(sum2), .cout(b1_cout));  // open: cin
  FullAdder1bit u_b2 (.a(sum2), .b(undriven_2), .sum(b2_sum), .cout(b2_cout));  // open: cin
  FullAdder1bit u_b3 (.a(b2_sum), .b(undriven_3), .sum(b3_sum), .cout(cout));  // open: cin

  assign sum4 = cout;
  // also tied to VCC on the sheet: sum1
endmodule

module FullAdder1bit (
  input  a,
  input  b,
  input  cin,
  output sum,
  output cout
);

  wire and_1_out, and_2_out, and_3_out, and_4_out, not_1_out, not_2_out;

  not not_1 (not_1_out, b);
  not not_2 (not_2_out, cin);
  and and_1 (and_1_out, a, cin);
  and and_2 (and_2_out, a, b);
  and and_3 (and_3_out, b, cin);
  and and_4 (and_4_out, a, not_1_out, not_2_out);
  or or_1 (cout, and_1_out, and_2_out);
  or or_2 (sum, and_3_out, and_4_out);
endmodule
