// Logisim project 6651071076_LAB1_5.circ as structural Verilog: 2 circuits, main circuit main
module main (
  input  [3:0] a,
  input  [3:0] b
);

  Comparator1bit comparator1bit_1 (.gt(a[1]), .eq(a[3]));  // open: a, b, lt
  Comparator1bit comparator1bit_2 (.eq(b[1]), .lt(b[3]));  // open: a, b, gt
  Comparator1bit comparator1bit_3 (.gt(a[2]), .eq(a[0]));  // open: a, b, lt
  Comparator1bit comparator1bit_4 (.gt(b[2]), .eq(b[2]));  // open: a, b, lt

  assign b[0] = b[2];
endmodule

module Comparator1bit (
  input  a,
  input  b,
  output gt,
  output eq,
  output lt
);

  wire and_2_out, and_3_out, not_1_out, not_2_out, not_3_out, not_4_out;

  not not_1 (not_1_out, b);
  not not_2 (not_2_out, a);
  not not_3 (not_3_out, b);
  not not_4 (not_4_out, a);
  and and_1 (gt, a, not_1_out);
  and and_2 (and_2_out, not_2_out, not_3_out);
  and and_3 (and_3_out, a, b);
  and and_4 (lt, not_4_out, b);
  or or_1 (eq, and_2_out, and_3_out);
endmodule
