// Logisim project 6651071076_LAB1_6.circ as structural Verilog: 1 circuit, main circuit main
module main (
  input  reset,
  output out_2,
  output out_3,
  output out_4,
  output out_5
);

  wire q1_q, q1_qn, q2_q, q2_qn, q3_q, q3_qn, q4_q, q4_qn;

  D_Flip_Flop q1 (.Q(q1_q), .Qn(q1_qn), .en(reset), .reset(q1_qn));  // open: clk, D, preset
  Clock clock_1 ();  // open: out
  D_Flip_Flop q2 (.Q(q2_q), .Qn(q2_qn), .preset(reset), .reset(q2_qn));  // open: clk, D, en
  D_Flip_Flop q3 (.Q(q3_q), .Qn(q3_qn), .preset(reset), .reset(q3_qn));  // open: clk, D, en
  D_Flip_Flop q4 (.Q(q4_q), .Qn(q4_qn), .preset(reset), .reset(q4_qn));  // open: clk, D, en
endmodule
