// Logisim project 6651071076_LAB1_7.circ as structural Verilog: 1 circuit, main circuit 6651071076_LAB1_7
module _6651071076_LAB1_7 (
  input  [2:0] Addr_2_0,
  input  [3:0] Data_in_3_0,
  input  Load_Write,
  output [3:0] Data_out_3_0
);

  wire Clock_out;

  Clock Clock (.out(Clock_out));
  // RAM #(.addrWidth(3), .dataWidth(4), .bus("separate")) ram_1: pin names not known; wires that end beside it: Addr_2_0, Data_in_3_0, Load_Write, 1'b1, Clock_out, 1'b1, Data_out_3_0
endmodule
